# Fritzing sketch schematic (saved by Fritzing 0.9.4)
circuit board: 12.5cm x 15cm
breadboards: 2

parts:
  U1 = atmega328 [package=dip]
  ESP8266 = ESP8266 WiFi Module [part_number=ESP8266]
  RB_G-1 = Resistor [tolerance=±5% resistance=10k package=THT]
  RB1-2 = Resistor [tolerance=±5% resistance=2.2k package=THT]
  RB2-3 = Resistor [tolerance=±5% resistance=2.2k package=THT]
  RB3-4 = Resistor [tolerance=±5% resistance=2.2k package=THT]
  RB4-5 = Resistor [tolerance=±5% resistance=2.2k package=THT]
  XTAL1 = Crystal [frequency="16 Mhz" package=THT]
  R_AVR_Reset = Resistor [tolerance=±5% resistance=10k package=THT]
  Main_Cap = Electrolytic Capacitor [capacitance=10µF package="100 mil [THT, electrolytic]"]
  RST-RX-TX_Headers = male pin header, 3 pins [form="♂ (male)"]
  D11-D12-D13_Headers = male pin header, 3 pins [form="♂ (male)"]
  R_TFT_Backlight = Resistor [tolerance=±5% resistance=47 package=THT]
  R_TFT_Reset_L = Resistor [tolerance=±5% resistance=270 package=THT]
  R_TFT_A0_L = Resistor [tolerance=±5% resistance=270 package=THT]
  R_TFT_SDA_L = Resistor [tolerance=±5% resistance=270 package=THT]
  R_TFT_SCL_L = Resistor [tolerance=±5% resistance=270 package=THT]
  R_TFT_CS_L = Resistor [tolerance=±5% resistance=270 package=THT]
  R_TFT_Reset_H = Resistor [tolerance=±5% resistance=500 package=THT]
  R_TFT_A0_H = Resistor [tolerance=±5% resistance=500 package=THT]
  R_TFT_SDA_H = Resistor [tolerance=±5% resistance=500 package=THT]
  R_TFT_SCL_H = Resistor [tolerance=±5% resistance=500 package=THT]
  R_TFT_CS_H = Resistor [tolerance=±5% resistance=500 package=THT]
  B1 = Tactile Switch Buttons - 12mm Square [package=tactile-pth-12mm]
  B2 = Tactile Switch Buttons - 12mm Square [package=tactile-pth-12mm]
  B4 = Tactile Switch Buttons - 12mm Square [package=tactile-pth-12mm]
  B3 = Tactile Switch Buttons - 12mm Square [package=tactile-pth-12mm]
  B5 = Tactile Switch Buttons - 12mm Square [package=tactile-pth-12mm]
  R_ESP_GPIO0 = Resistor [tolerance=±5% resistance=10k package=THT]
  R_ESP_RX_CH_PD = Resistor [tolerance=±5% resistance=10k package=THT]
  R_ESP_RST = Resistor [tolerance=±5% resistance=10k package=THT]
  ESP_Prog_Button = male pin header, 2 pins [form="♂ (male)"]
  ESP_RST_Button = male pin header, 2 pins [form="♂ (male)"]
  R_ESP_RX_L = Resistor [tolerance=±5% resistance=1k package=THT]
  R_ESP_RX_H = Resistor [tolerance=±5% resistance=2k package=THT]
  ESP_Debug_Header_(TX) = male pin header, 1 pin [form="♂ (male)"]
  ESP_RX_Header_/_Jumper = male pin header, 2 pins [form="♂ (male)"]
  ESP_TX_Header_/_Jumper = male pin header, 2 pins [form="♂ (male)"]
  Temp_Strip = male pin header, 3 pins [form="♂ (male)"]
  Power_Strip_(5V) = male pin header, 2 pins [form="♂ (male)"]
  R_Temp = Resistor [tolerance=±5% resistance=4.7k package=THT]
  Relay_Strip = male pin header, 3 pins [form="♂ (male)"]
  j = male pin header, 1 pin [form="♂ (male)"]
  j_2 = male pin header, 1 pin [form="♂ (male)"]
  j_3 = male pin header, 1 pin [form="♂ (male)"]
  j_4 = male pin header, 1 pin [form="♂ (male)"]
  j_5 = male pin header, 1 pin [form="♂ (male)"]
  j_6 = male pin header, 1 pin [form="♂ (male)"]
  j_7 = male pin header, 1 pin [form="♂ (male)"]
  j_8 = male pin header, 1 pin [form="♂ (male)"]
  j_9 = male pin header, 1 pin [form="♂ (male)"]
  j_10 = male pin header, 1 pin [form="♂ (male)"]
  j1 = male pin header, 1 pin [form="♂ (male)"]
  j2 = male pin header, 1 pin [form="♂ (male)"]
  j5 = male pin header, 1 pin [form="♂ (male)"]
  j6 = male pin header, 1 pin [form="♂ (male)"]
  j4 = male pin header, 1 pin [form="♂ (male)"]
  j3 = male pin header, 1 pin [form="♂ (male)"]
  j_11 = male pin header, 1 pin [form="♂ (male)"]
  j_12 = male pin header, 1 pin [form="♂ (male)"]
  j_13 = male pin header, 1 pin [form="♂ (male)"]
  j_14 = male pin header, 1 pin [form="♂ (male)"]
  j_15 = male pin header, 1 pin [form="♂ (male)"]
  j_16 = male pin header, 1 pin [form="♂ (male)"]
  j_17 = male pin header, 1 pin [form="♂ (male)"]
  j_18 = male pin header, 1 pin [form="♂ (male)"]
  j_19 = male pin header, 1 pin [form="♂ (male)"]
  j_20 = male pin header, 1 pin [form="♂ (male)"]
  j_21 = male pin header, 1 pin [form="♂ (male)"]
  j_22 = male pin header, 1 pin [form="♂ (male)"]
  j_23 = male pin header, 1 pin [form="♂ (male)"]
  j_24 = male pin header, 1 pin [form="♂ (male)"]
  j_25 = male pin header, 1 pin [form="♂ (male)"]
  j_26 = male pin header, 1 pin [form="♂ (male)"]
  j_27 = male pin header, 1 pin [form="♂ (male)"]
  j_28 = male pin header, 1 pin [form="♂ (male)"]
  j_29 = male pin header, 1 pin [form="♂ (male)"]
  j_30 = male pin header, 1 pin [form="♂ (male)"]
  j_31 = male pin header, 1 pin [form="♂ (male)"]
  j_32 = male pin header, 1 pin [form="♂ (male)"]
  j_33 = male pin header, 1 pin [form="♂ (male)"]
  j_34 = male pin header, 1 pin [form="♂ (male)"]
  j_35 = male pin header, 1 pin [form="♂ (male)"]
  j_36 = male pin header, 1 pin [form="♂ (male)"]
  j_37 = male pin header, 1 pin [form="♂ (male)"]
  j_38 = male pin header, 1 pin [form="♂ (male)"]
  j_39 = male pin header, 1 pin [form="♂ (male)"]
  j_40 = male pin header, 1 pin [form="♂ (male)"]
  j_41 = male pin header, 1 pin [form="♂ (male)"]
  j_42 = male pin header, 1 pin [form="♂ (male)"]
  j7 = male pin header, 1 pin [form="♂ (male)"]
  AMS_IN = male pin header, 2 pins [form="♂ (male)"]
  TFT = mystery part, 16 pins [chip_label="TFT Display (128x160)"]
  AMS_OUT = male pin header, 2 pins [form="♂ (male)"]
  C1a = male pin header, 1 pin [form="♂ (male)"]
  C1b = male pin header, 1 pin [form="♂ (male)"]
  C2a = male pin header, 1 pin [form="♂ (male)"]
  C2b = male pin header, 1 pin [form="♂ (male)"]

nets (from the pcb view):
  N1: U1.RESET, R_AVR_Reset.Pin_0, RST-RX-TX_Headers.pin1
  N2: U1.D0_(RX), RST-RX-TX_Headers.pin2
  N3: U1.D1_(TX), RST-RX-TX_Headers.pin3
  N4: U1.D2, Temp_Strip.pin3, R_Temp.Pin_1, j_27.pin1, j_29.pin1
  N5: U1.D3_(PWM), U1.A0, RB_G-1.Pin_1, RB2-3.Pin_0, B1.1, B1.3, B2.1, B2.3
  N6: U1.D4, R_TFT_Reset_L.Pin_1, R_TFT_Reset_H.Pin_0, j_6.pin1, j1.pin1
  N7: U1.VCC, U1.AVCC, RB4-5.Pin_0, R_AVR_Reset.Pin_1, Main_Cap.+, B5.2, B5.4, Temp_Strip.pin1, Power_Strip_(5V).pin2, R_Temp.Pin_0, Relay_Strip.pin1, j_5.pin1, j_7.pin1, j_28.pin1, j_34.pin1, j_41.pin1, j_42.pin1, AMS_IN.pin1, TFT.pin2
  N8: U1.GND, RB_G-1.Pin_0, Main_Cap.-, R_TFT_Reset_H.Pin_1, R_TFT_A0_H.Pin_1, R_TFT_SDA_H.Pin_1, R_TFT_SCL_H.Pin_1, R_TFT_CS_H.Pin_1, Power_Strip_(5V).pin1, j_14.pin1, j_15.pin1, j_16.pin1, j_17.pin1, j_18.pin1, j_19.pin1, j_37.pin1, j_38.pin1, j_39.pin1, j_40.pin1, AMS_IN.pin2, TFT.pin1, TFT.pin16, C1b.pin1
  N9: U1.XLAT1, XTAL1.pin_1, C2a.pin1
  N10: U1.XLAT2, XTAL1.pin_0, C1a.pin1
  N11: U1.D5_(PWM), R_TFT_A0_L.Pin_1, R_TFT_A0_H.Pin_0, j_4.pin1, j2.pin1
  N12: U1.D6_(PWM), R_TFT_CS_L.Pin_1, R_TFT_CS_H.Pin_0, j_3.pin1, j5.pin1
  N13: U1.D7, Relay_Strip.pin3, j_32.pin1, j_33.pin1
  N14: U1.D8, ESP_TX_Header_/_Jumper.pin1, j.pin1, j_2.pin1
  N15: U1.D9_(PWM), ESP_RX_Header_/_Jumper.pin1
  N16: U1.D10_(PWM), R_TFT_Backlight.Pin_1, j_9.pin1, j6.pin1
  N17: U1.D11_(PWM), D11-D12-D13_Headers.pin1, R_TFT_SDA_L.Pin_1, R_TFT_SDA_H.Pin_0, j_10.pin1, j3.pin1
  N18: U1.D12, D11-D12-D13_Headers.pin2
  N19: U1.D13, D11-D12-D13_Headers.pin3, R_TFT_SCL_L.Pin_1, R_TFT_SCL_H.Pin_0, j_8.pin1, j4.pin1
  N20: U1.AREF, j7.pin1
  N21: ESP8266.RXD, R_ESP_RX_L.Pin_1, R_ESP_RX_H.Pin_0, j_11.pin1, j_12.pin1
  N22: ESP8266.VCC, R_ESP_GPIO0.Pin_1, R_ESP_RX_CH_PD.Pin_1, R_ESP_RST.Pin_1, AMS_OUT.pin1
  N23: ESP8266.GPIO_0, R_ESP_GPIO0.Pin_0, ESP_Prog_Button.pin2
  N24: ESP8266.RST, R_ESP_RST.Pin_0, ESP_RST_Button.pin1
  N25: ESP8266.GPIO_2, ESP_Debug_Header_(TX).pin1
  N26: ESP8266.CH_PD, R_ESP_RX_CH_PD.Pin_0
  N27: ESP8266.GND, ESP_Prog_Button.pin1, ESP_RST_Button.pin2, R_ESP_RX_H.Pin_1, j_13.pin1, j_20.pin1, j_21.pin1, j_22.pin1, j_23.pin1, j_24.pin1, j_25.pin1, j_26.pin1, AMS_OUT.pin2
  N28: ESP8266.TXD, ESP_TX_Header_/_Jumper.pin2
  N29: RB1-2.Pin_0, RB3-4.Pin_1, B2.2, B2.4, B3.1, B3.3
  N30: RB1-2.Pin_1, B1.2, B1.4
  N31: RB2-3.Pin_1, RB4-5.Pin_1, B4.1, B4.3, B3.2, B3.4
  N32: RB3-4.Pin_0, B4.2, B4.4, B5.1, B5.3
  N33: R_TFT_Backlight.Pin_0, TFT.pin15
  N34: R_TFT_Reset_L.Pin_0, TFT.pin6
  N35: R_TFT_A0_L.Pin_0, TFT.pin7
  N36: R_TFT_SDA_L.Pin_0, TFT.pin8
  N37: R_TFT_SCL_L.Pin_0, TFT.pin9
  N38: R_TFT_CS_L.Pin_0, TFT.pin10
  N39: R_ESP_RX_L.Pin_0, ESP_RX_Header_/_Jumper.pin2
  N40: Temp_Strip.pin2, Relay_Strip.pin2, j_30.pin1, j_31.pin1, j_35.pin1, j_36.pin1, C2b.pin1

custom parts:
  ESP8266 WiFi Module: Generic WiFi Module based on the ESP8266 with onboard PCB antenna and UART communications
  Tactile Switch Buttons - 12mm Square: Medium-sized clicky momentary switches are standard input "buttons" on electronic projects. These work best in a PCB but can be used on a solderless breadboard as shown in this tutorial. The pins are normally open (disconnected) and when the button is pressed they are momentarily closed. They come in a pack of 10, they're pretty handy so you'll want to keep them around. You can find an EAGLE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
